# Fritzing sketch envduino (saved by Fritzing 0.8.0b)
breadboards: 2

parts:
  DHT1 = DHT22 Humidity and Temperature Sensor
  BMP1 = BMP085 Breakout
  Arduino1 = Arduino Mega
  10k = Resistor [tolerance=±5% resistance=10k package=THT]

nets:
  VDD: DHT1.VDD, Arduino1.+5V, 10k.Pin_1
  N1: DHT1.DATA, Arduino1.D2, 10k.Pin_0
  N2: BMP1.SCL, Arduino1.D21
  N3: BMP1.SDA, Arduino1.D20

custom parts:
  BMP085 Breakout: A breakout for the BMP085 barometric pressure and temperature sensor
